# Fritzing sketch Blinkety_Blink (saved by Fritzing 0.6.2b)
breadboards: 1

parts:
  LED1 = RGB LED (com. cathode, rbg) [package="5 mm [THT]"]
  R1 = Resistor [tolerance=±20% resistance=330 package=THT]
  R2 = Resistor [tolerance=±20% resistance=330 package=THT]
  R3 = Resistor [tolerance=±20% resistance=330 package=THT]
  Arduino1 = Arduino
  R4 = Rotary Potentiometer (Small) [maximum_resistance=100kΩ]

nets:
  N1: LED1.red_anode, R3.Pin_1
  N2: LED1.common_cathode, Arduino1.GND, R4.leg1
  N3: LED1.blue_anode, R1.Pin_0
  N4: LED1.green_anode, R2.Pin_0
  N5: R1.Pin_1, Arduino1.D5
  N6: R2.Pin_1, Arduino1.D6
  N7: R3.Pin_0, Arduino1.D3
  N8: Arduino1.+5V, R4.leg2
  N9: Arduino1.A0, R4.wiper
